# Fritzing sketch GlowingHouse (saved by Fritzing 0.9.9b)
breadboards: 1

parts:
  J1 = Basic Force Sensing Resistor (FSR) [package=THT]
  J2 = Basic Force Sensing Resistor (FSR) [package=THT]
  J3 = Basic Force Sensing Resistor (FSR) [package=THT]
  Part1 = Arduino Uno (Rev3)
  M1 = ac light dimmer 3terminal
  R1 = Resistor [tolerance=±5% resistance=220 package="1206 [SMD]"]
  LED1 = LEDs [package=led10mm]

nets:
  N1: J1.pin_0, J2.pin_0, J3.pin_0, Part1.A0, R1.Pin_0
  5V: J1.pin_1, J2.pin_1, J3.pin_1, Part1.5V, M1.VCC
  N2: Part1.D12/MISO, M1.PWM
  N3: Part1.D2, M1.Z-C
  GND: Part1.GND, M1.GND, R1.Pin_1
  N4: M1.OUT, LED1.C

custom parts:
  ac light dimmer 3terminal: ac light dimmer module 3 output terminals.
  LEDs: LEDs Standard schematic elements and footprints for 5mm, 3mm, 1206, and 0603 sized LEDs. 5mm - Spark Fun Electronics SKU : COM-00529 (and others)
